# Fritzing sketch Recep_prot (saved by Fritzing 0.9.3b)
perfboards: 1

parts:
  ESP32_LORA1 = IC, DIP package, 36 pins [chip_label=ESP32]  # not connected
  BAT = Battery Holders [package=battery-aa]
  SW1 = DIP SWITCH [package=dipswitch-02]
  button_conn = female pin header, 4 pins [form="♀ (female)"]
  Piezo1 = Piezo Speaker - PC Mount [part_number=COM-07950]
  J2 = female pin header, 18 pins [form="♀ (female)"]
  J3 = female pin header, 18 pins [form="♀ (female)"]
  Bat_conn = female pin header, 2 pins [form="♀ (female)"]
  R1 = Resistor [tolerance=±5% resistance=100 package=THT]
  S2 = Round Pushbutton
  LED1 = LED - 5mm [color="Red (633nm)" package="5 mm [THT]"]
  R2 = Resistor [tolerance=±5% resistance=220 package=THT]

nets:
  GND: BAT.-, button_conn.pin1, Piezo1.GND, J2.pin1, J3.pin1, Bat_conn.pin2, LED1.cathode
  N1: BAT.+, button_conn.pin3, S2.leg0
  N2: SW1.1, button_conn.pin2, R2.Pin_0
  N3: SW1.2, R1.Pin_0
  N4: SW1.3, J2.pin9
  N5: SW1.4, LED1.anode
  N6: button_conn.pin4, Bat_conn.pin1, S2.leg1
  N7: Piezo1.VCC, R1.Pin_1
  N8: J2.pin15, R2.Pin_1

custom parts:
  Piezo Speaker - PC Mount: This is a small 12mm round speaker that operates around the audible 2kHz range. You can use these speakers to create simple music or user interfaces. Each speaker is PTH solderable and requires an operating voltage of 3.5-5V with a mean current of 35mA max. These speakers also have a typical sound output of 95 dBA and a coil resistance of 42 ±6.3 ohms.
